# Fritzing sketch FSK (saved by Fritzing 0.6.4b)
breadboards: 1

parts:
  C1 = Ceramic Capacitor [capacitance=0.47µF package="100 mil [THT, multilayer]"]
  R1 = Resistor [tolerance=±5% resistance=100k package=THT]
  R2 = Resistor [tolerance=±5% resistance=100k package=THT]
  Arduino1 = Arduino
  C2 = Ceramic Capacitor [capacitance=0.47µF package="100 mil [THT, multilayer]"]

nets:
  N1: C1.1, R1.Pin_0, R2.Pin_0, Arduino1.D6, C2.0
  N2: R1.Pin_1, Arduino1.3V3
  N3: R2.Pin_1, Arduino1.GND, C2.1

notes:
  Audio GND
  Audio L or R
